// Logisim project main.circ as structural Verilog: 2 circuits, main circuit main
module main (
  output [39:0] out_1,
  output [7:0] out_2,
  output [3:0] out_3,
  output [3:0] out_4,
  output [15:0] out_5,
  output [15:0] out_6,
  output [8:0] out_7
);

  wire ALLOW_WRITE, and_1_out, ARG1_TYPE, ARG2_TYPE, CLK, comparator_1_eq, demultiplexer_1_out1,
       demultiplexer_2_out0, demultiplexer_2_out1, demultiplexer_2_out2, demultiplexer_2_out3,
       demultiplexer_2_out4, demultiplexer_2_out5, demultiplexer_2_out6, demultiplexer_2_out7,
       demultiplexer_3_out1, demultiplexer_4_out1, demultiplexer_5_out2, not_1_out, or_1_out, RESET;
  wire [2:0] bit_extender_1_out, bit_extender_2_out, multiplexer_2_out;
  wire [15:0] adder_1_out, ADDR_MEM, ARG1_REG_VALUE, ARG2_REG_VALUE, CST_R0, CST_R1, divider_1_out,
       multiplexer_5_out, multiplexer_6_out, multiplier_1_out, R2_q, R2_RES, R3_q, R4_q, R5_q, R6_q, R7_q,
       SAVE_VALUE, subtractor_1_out, VALUE_MEM_D, VALUE_MEM_Q;

  Button button_1 (.out(RESET));
  Clock clock_1 (.out(CLK));
  Adder #(.width(16)) adder_1 (.a(CST_R0), .b(CST_R1), .out(adder_1_out));  // open: cin, cout
  Subtractor #(.width(16)) subtractor_1 (.a(CST_R0), .b(CST_R1), .out(subtractor_1_out));  // open: bin, bout
  Multiplier #(.width(16)) multiplier_1 (.a(CST_R0), .b(CST_R1), .out(multiplier_1_out));  // open: cin, cout
  Divider #(.width(16)) divider_1 (.a(CST_R0), .b(CST_R1), .out(divider_1_out));  // open: upper, rem
  is_memaddr is_memaddr_1 (.in_1(out_1[31:16]), .out_2(ARG1_TYPE));
  is_memaddr is_memaddr_2 (.in_1(out_1[15:0]), .out_2(ARG2_TYPE));
  not not_1 (not_1_out, CLK);
  Multiplexer #(.select(2), .width(16)) multiplexer_1 (
    .in0(adder_1_out), .in1(subtractor_1_out), .in2(multiplier_1_out), .in3(divider_1_out), .out(R2_RES),
    .sel(out_1[33:32]));
  Counter #(.max('h1ff), .width(9)) counter_1 (
    .clr(RESET), .clk(not_1_out), .Q(out_7));  // open: load, up, count, D, carry
  ROM #(.addrWidth(9), .dataWidth(40)) PROG (.addr(out_7), .data(out_1));
  Demultiplexer #(.select(2)) demultiplexer_1 (
    .out1(demultiplexer_1_out1), .in(1'b1), .sel(out_1[37:36]));  // open: out0, out2, out3
  Demultiplexer #(.select(3)) demultiplexer_2 (
    .out0(demultiplexer_2_out0), .out1(demultiplexer_2_out1), .out2(demultiplexer_2_out2),
    .out3(demultiplexer_2_out3), .out4(demultiplexer_2_out4), .out5(demultiplexer_2_out5),
    .out6(demultiplexer_2_out6), .out7(demultiplexer_2_out7), .in(1'b1), .sel(multiplexer_2_out));
  Multiplexer #(.width(3)) multiplexer_2 (
    .in0(out_1[2:0]), .in1(3'b010), .out(multiplexer_2_out), .sel(demultiplexer_1_out1));
  Register #(.trigger("high"), .width(16)) R0 (
    .D(SAVE_VALUE), .en(demultiplexer_2_out0), .clk(and_1_out), .Q(CST_R0), .clr(RESET));
  Register #(.trigger("high"), .width(16)) R1 (
    .D(SAVE_VALUE), .en(demultiplexer_2_out1), .clk(and_1_out), .Q(CST_R1), .clr(RESET));
  Register #(.trigger("high"), .width(16)) R2 (
    .D(SAVE_VALUE), .en(demultiplexer_2_out2), .clk(and_1_out), .Q(R2_q), .clr(RESET));
  Register #(.trigger("high"), .width(16)) R3 (
    .D(SAVE_VALUE), .en(demultiplexer_2_out3), .clk(and_1_out), .Q(R3_q), .clr(RESET));
  Register #(.trigger("high"), .width(16)) R4 (
    .D(SAVE_VALUE), .en(demultiplexer_2_out4), .clk(and_1_out), .Q(R4_q), .clr(RESET));
  Register #(.trigger("high"), .width(16)) R5 (
    .D(SAVE_VALUE), .en(demultiplexer_2_out5), .clk(and_1_out), .Q(R5_q), .clr(RESET));
  Register #(.trigger("high"), .width(16)) R6 (
    .D(SAVE_VALUE), .en(demultiplexer_2_out6), .clk(and_1_out), .Q(R6_q), .clr(RESET));
  Register #(.trigger("high"), .width(16)) R7 (
    .D(SAVE_VALUE), .en(demultiplexer_2_out7), .clk(and_1_out), .Q(R7_q), .clr(RESET));
  and and_1 (and_1_out, ~ARG2_TYPE, ALLOW_WRITE);  // AND_Gate
  Demultiplexer #(.select(2)) demultiplexer_3 (
    .out1(demultiplexer_3_out1), .in(1'b1), .sel(out_1[37:36]));  // open: out0, out2, out3
  Comparator #(.width(4)) comparator_1 (.a(out_1[39:36]), .b(4'b0000), .eq(comparator_1_eq));  // open: gt, lt
  Multiplexer #(.select(3), .width(16)) multiplexer_3 (
    .in0(CST_R0), .in1(CST_R1), .in2(R2_q), .in3(R3_q), .in4(R4_q), .in5(R5_q), .in6(R6_q), .in7(R7_q),
    .out(ARG1_REG_VALUE), .sel(bit_extender_2_out));
  Multiplexer #(.select(3), .width(16)) multiplexer_4 (
    .in0(CST_R0), .in1(CST_R1), .in2(R2_q), .in3(R3_q), .in4(R4_q), .in5(R5_q), .in6(R6_q), .in7(R7_q),
    .out(ARG2_REG_VALUE), .sel(bit_extender_1_out));
  or or_1 (or_1_out, comparator_1_eq, demultiplexer_3_out1);
  Bit_Extender #(.in_width(16), .out_width(3)) bit_extender_1 (.in(out_1[15:0]), .out(bit_extender_1_out));
  and and_2 (ALLOW_WRITE, or_1_out, CLK);
  Bit_Extender #(.in_width(16), .out_width(3)) bit_extender_2 (.in(out_1[31:16]), .out(bit_extender_2_out));
  Demultiplexer #(.select(2)) demultiplexer_4 (
    .out1(demultiplexer_4_out1), .in(1'b1), .sel(out_1[37:36]));  // open: out0, out2, out3
  RAM #(.addrWidth(16), .dataWidth(16)) MEMORY (
    .addr(ADDR_MEM), .we(ARG2_TYPE), .oe(1'b1), .clk(ALLOW_WRITE), .din(VALUE_MEM_D), .dout(VALUE_MEM_Q));
  Multiplexer #(.width(16)) multiplexer_5 (
    .in0(ARG1_REG_VALUE), .in1(VALUE_MEM_Q), .out(multiplexer_5_out), .sel(ARG1_TYPE));
  Multiplexer #(.width(16)) multiplexer_6 (
    .in0(multiplexer_5_out), .in1(out_1[31:16]), .out(multiplexer_6_out), .sel(demultiplexer_5_out2));
  Demultiplexer #(.select(2)) demultiplexer_5 (
    .out2(demultiplexer_5_out2), .in(1'b1), .sel(out_1[33:32]));  // open: out0, out1, out3
  Multiplexer #(.width(16)) multiplexer_7 (
    .in0(multiplexer_6_out), .in1(R2_RES), .out(SAVE_VALUE), .sel(demultiplexer_4_out1));
  Multiplexer #(.width(16)) multiplexer_8 (.in0(out_1[31:16]), .in1(out_1[15:0]), .out(ADDR_MEM), .sel(CLK));

  assign out_2 = out_1[39:32];
  assign out_3 = out_1[39:36];
  assign out_4 = out_1[35:32];
  assign out_5 = out_1[31:16];
  assign out_6 = out_1[15:0];

  // Other names for the same wires on the sheet: INT_ARG2[15:0] = out_1[15:0]; INT_BITFIELD[39:0] = out_1;
  //   INT_ARG1[15:0] = out_1[31:16]; INT_OP_TYPE2[3:0] = out_1[35:32]; INT_OPCODE[7:0] = out_1[39:32];
  //   INT_OP_TYPE1[3:0] = out_1[39:36]; INT_COUNTER[8:0] = out_7; MEM_WE = ARG2_TYPE

  // Notes on the sheet:
  //   contents of PROG (hex, n*v repeats v):
  //   200320000 200010001 200000003 1100000000 100020004 100030001 1000000000 100020001 100040000
  //   2100000000 3000030000 100010020 200410050
endmodule

module is_memaddr (
  input  [15:0] in_1,
  output out_2
);

  Comparator #(.width(16)) comparator_1 (.a(in_1), .b(16'h8), .gt(out_2));  // open: eq, lt
endmodule
